// Logisim project m8b.circ as structural Verilog: 3 circuits, main circuit Multiplicador
module Multiplicador (
  input  [7:0] M,
  input  [7:0] Q,
  input  Clock,
  input  Reset,
  output [7:0] A,
  output [7:0] Q_2
);

  wire comparator_1_lt, comparator_2_gt;
  wire [7:0] counter_1_q, M_q, multiplexer_1_out, multiplexer_2_out;
  wire [7:1] n8_bits_full_adder_1_r_2;
  wire [7:7] n8_bits_full_adder_1_r;
  wire [16:16] n8_bits_full_adder_1_c_out;

  Counter counter_1 (.count(comparator_2_gt), .Q(counter_1_q), .clk(Clock), .clr(Reset));  // open: load, D, carry
  Comparator comparator_1 (.a({8{1'b0}}), .b(counter_1_q), .lt(comparator_1_lt));  // open: gt, eq
  Comparator comparator_2 (.a(8'h9), .b(counter_1_q), .gt(comparator_2_gt));  // open: eq, lt
  Multiplexer #(.width(8), .enable("false")) multiplexer_1 (
    .in0(Q), .in1({n8_bits_full_adder_1_r[7], Q_2[7:1]}), .out(multiplexer_1_out), .sel(comparator_1_lt));
  Register u_M (.D(M), .en(comparator_2_gt), .Q(M_q), .clk(Clock), .clr(Reset));
  Register u_Q (.D(multiplexer_1_out), .en(comparator_2_gt), .Q(Q_2), .clk(Clock), .clr(Reset));
  Register u_A (
    .D({n8_bits_full_adder_1_c_out[16], n8_bits_full_adder_1_r_2}), .en(comparator_2_gt), .Q(A), .clk(Clock),
    .clr(Reset));
  Multiplexer #(.width(8), .enable("false")) multiplexer_2 (
    .in0({8{1'b0}}), .in1(M_q), .out(multiplexer_2_out), .sel(Q_2[0]));
  _8_bits_full_adder u_8_bits_full_adder_1 (
    .Q(multiplexer_2_out), .M(A), .R({n8_bits_full_adder_1_r_2, n8_bits_full_adder_1_r[7]}),
    .C_OUT(n8_bits_full_adder_1_c_out[16]));
endmodule

module full_adder (
  input  Q,
  input  M,
  input  C_IN,
  output R,
  output C_OUT
);

  wire and_1_out, and_2_out, and_3_out, xor_1_out;

  xor xor_1 (xor_1_out, Q, M);
  and and_1 (and_1_out, Q, M);
  and and_2 (and_2_out, Q, C_IN);
  and and_3 (and_3_out, M, C_IN);
  xor xor_2 (R, xor_1_out, C_IN);
  or or_1 (C_OUT, and_1_out, and_2_out, and_3_out);
endmodule

module _8_bits_full_adder (
  input  [7:0] Q,
  input  [7:0] M,
  output [7:0] R,
  output C_OUT
);

  wire full_adder_1_c_out, full_adder_2_c_out, full_adder_3_c_out, full_adder_4_c_out, full_adder_5_c_out,
       full_adder_6_c_out, full_adder_7_c_out;

  full_adder full_adder_1 (.Q(Q[0]), .M(M[0]), .C_IN(1'b0), .R(R[0]), .C_OUT(full_adder_1_c_out));
  full_adder full_adder_2 (.Q(Q[1]), .M(M[1]), .C_IN(full_adder_1_c_out), .R(R[1]), .C_OUT(full_adder_2_c_out));
  full_adder full_adder_3 (.Q(Q[2]), .M(M[2]), .C_IN(full_adder_2_c_out), .R(R[2]), .C_OUT(full_adder_3_c_out));
  full_adder full_adder_4 (.Q(Q[3]), .M(M[3]), .C_IN(full_adder_3_c_out), .R(R[3]), .C_OUT(full_adder_4_c_out));
  full_adder full_adder_5 (.Q(Q[4]), .M(M[4]), .C_IN(full_adder_4_c_out), .R(R[4]), .C_OUT(full_adder_5_c_out));
  full_adder full_adder_6 (.Q(Q[5]), .M(M[5]), .C_IN(full_adder_5_c_out), .R(R[5]), .C_OUT(full_adder_6_c_out));
  full_adder full_adder_7 (.Q(Q[6]), .M(M[6]), .C_IN(full_adder_6_c_out), .R(R[6]), .C_OUT(full_adder_7_c_out));
  full_adder full_adder_8 (.Q(Q[7]), .M(M[7]), .C_IN(full_adder_7_c_out), .R(R[7]), .C_OUT(C_OUT));
endmodule
