// Logisim project multiplicador32float.circ as structural Verilog: 3 circuits, main circuit 32float
module _32float (
  input  [31:0] A,
  input  [31:0] B,
  output [31:0] R,
  output O,
  output U
);

  wire comparator_1_eq, comparator_2_eq, or_1_out, or_2_out, soma_espoente_1_overflow,
       soma_espoente_1_underflow;
  wire [7:0] soma_espoente_1_expoente;
  wire [22:0] multiplica_mantissa_1_mantissa;
  wire [31:31] xor_1_out;

  Soma_Espoente soma_espoente_1 (
    .A(A[30:23]), .B(B[30:23]), .Expoente(soma_espoente_1_expoente), .Overflow(soma_espoente_1_overflow),
    .Underflow(soma_espoente_1_underflow));
  Multiplica_Mantissa multiplica_mantissa_1 (.A(A[22:0]), .B(B[22:0]), .Mantissa(multiplica_mantissa_1_mantissa));
  Comparator #(.width(31)) comparator_1 (.a(A[30:0]), .b({31{1'b0}}), .eq(comparator_1_eq));  // open: gt, lt
  Comparator #(.width(31)) comparator_2 (.a(A[30:0]), .b({31{1'b0}}), .eq(comparator_2_eq));  // open: gt, lt
  xor xor_1 (xor_1_out[31], A[31], B[31]);
  or or_1 (or_1_out, comparator_1_eq, comparator_2_eq);
  or or_2 (or_2_out, soma_espoente_1_overflow, soma_espoente_1_underflow, or_1_out);
  Multiplexer #(.width(32), .enable("false")) multiplexer_1 (
    .in0({xor_1_out[31], soma_espoente_1_expoente, multiplica_mantissa_1_mantissa}), .in1({32{1'b0}}),
    .out(R), .sel(or_2_out));
  Multiplexer #(.enable("false")) multiplexer_2 (.in0(soma_espoente_1_overflow), .in1(1'b0), .out(O), .sel(or_1_out));
  Multiplexer #(.enable("false")) multiplexer_3 (.in0(soma_espoente_1_underflow), .in1(1'b0), .out(U), .sel(or_1_out));

  // Notes on the sheet:
  //   Expoente
  //   Mantissa
  //   Sinal
endmodule

module Soma_Espoente (
  input  [7:0] A,
  input  [7:0] B,
  output [7:0] Expoente,
  output Overflow,
  output Underflow
);
endmodule

module Multiplica_Mantissa (
  input  [22:0] A,
  input  [22:0] B,
  output [22:0] Mantissa
);
endmodule
