// Logisim project mult8bits.circ as structural Verilog: 3 circuits, main circuit Multiplicador
module Multiplicador (
  input  [7:0] M,
  input  [7:0] Q,
  input  Reset,
  output [15:0] R,
  output C_OUT
);

  wire bitselector_1_out, clock_1_out, comparator_1_gt, comparator_2_eq;
  wire [7:0] counter_1_q, M_q, multiplexer_1_out, multiplexer_2_out, shifter_1_out, somador_8_bits_1_r;
  wire [16:0] shifter_1_out_2;

  Counter counter_1 (.count(comparator_1_gt), .Q(counter_1_q), .clk(clock_1_out), .clr(Reset));  // open: load, D, carry
  Clock clock_1 (.out(clock_1_out));
  Comparator comparator_1 (.a(8'h9), .b(counter_1_q), .gt(comparator_1_gt));  // open: eq, lt
  Comparator comparator_2 (.a({8{1'b0}}), .b(counter_1_q), .eq(comparator_2_eq));  // open: gt, lt
  Multiplexer #(.width(8), .enable("false")) multiplexer_1 (
    .in0(shifter_1_out_2[7:0]), .in1(Q), .out(multiplexer_1_out), .sel(comparator_2_eq));
  Register u_M (.D(M), .en(comparator_1_gt), .Q(M_q), .clk(clock_1_out), .clr(Reset));
  Register A (.D(shifter_1_out), .en(comparator_1_gt), .Q(R[15:8]), .clk(clock_1_out), .clr(Reset));
  Register u_Q (.D(multiplexer_1_out), .en(comparator_1_gt), .Q(R[7:0]), .clk(clock_1_out), .clr(Reset));
  Multiplexer #(.width(8), .enable("false")) multiplexer_2 (
    .in0({8{1'b0}}), .in1(M_q), .out(multiplexer_2_out), .sel(bitselector_1_out));
  BitSelector bitselector_1 (.in(R[7:0]), .out(bitselector_1_out), .sel(3'b000));
  somador_8_bits somador_8_bits_1 (.A(multiplexer_2_out), .B(R[15:8]), .R(somador_8_bits_1_r), .C_OUT(C_OUT));
  Shifter #(.width(17), .shift("lr")) shifter_1 (
    .in({C_OUT, somador_8_bits_1_r, R[7:0]}), .\dist (5'b00001),
    .out({shifter_1_out_2[16], shifter_1_out, shifter_1_out_2[7:0]}));
endmodule

module somador_1_bit (
  input  A,
  input  B,
  input  C_IN,
  output R,
  output C_OUT
);

  wire and_1_out, and_2_out, and_3_out, xor_1_out;

  xor xor_1 (xor_1_out, A, B);
  and and_1 (and_1_out, A, B);
  and and_2 (and_2_out, A, C_IN);
  and and_3 (and_3_out, B, C_IN);
  xor xor_2 (R, xor_1_out, C_IN);
  or or_1 (C_OUT, and_1_out, and_2_out, and_3_out);
endmodule

module somador_8_bits (
  input  [7:0] A,
  input  [7:0] B,
  output [7:0] R,
  output C_OUT
);

  wire somador_1_bit_1_c_out, somador_1_bit_2_c_out, somador_1_bit_3_c_out, somador_1_bit_4_c_out,
       somador_1_bit_5_c_out, somador_1_bit_6_c_out, somador_1_bit_7_c_out;

  somador_1_bit somador_1_bit_1 (.A(A[0]), .B(B[0]), .C_IN(1'b0), .R(R[0]), .C_OUT(somador_1_bit_1_c_out));
  somador_1_bit somador_1_bit_2 (
    .A(A[1]), .B(B[1]), .C_IN(somador_1_bit_1_c_out), .R(R[1]), .C_OUT(somador_1_bit_2_c_out));
  somador_1_bit somador_1_bit_3 (
    .A(A[2]), .B(B[2]), .C_IN(somador_1_bit_2_c_out), .R(R[2]), .C_OUT(somador_1_bit_3_c_out));
  somador_1_bit somador_1_bit_4 (
    .A(A[3]), .B(B[3]), .C_IN(somador_1_bit_3_c_out), .R(R[3]), .C_OUT(somador_1_bit_4_c_out));
  somador_1_bit somador_1_bit_5 (
    .A(A[4]), .B(B[4]), .C_IN(somador_1_bit_4_c_out), .R(R[4]), .C_OUT(somador_1_bit_5_c_out));
  somador_1_bit somador_1_bit_6 (
    .A(A[5]), .B(B[5]), .C_IN(somador_1_bit_5_c_out), .R(R[5]), .C_OUT(somador_1_bit_6_c_out));
  somador_1_bit somador_1_bit_7 (
    .A(A[6]), .B(B[6]), .C_IN(somador_1_bit_6_c_out), .R(R[6]), .C_OUT(somador_1_bit_7_c_out));
  somador_1_bit somador_1_bit_8 (.A(A[7]), .B(B[7]), .C_IN(somador_1_bit_7_c_out), .R(R[7]), .C_OUT(C_OUT));
endmodule
